// Digital circuit Dflip-flop.dig as structural Verilog
module Dflip_flop (
  input  I,
  input  C,
  input  R,
  output Q,
  output nQ
);

  wire multiplexer_1_out, multiplexer_2_out;

  Multiplexer multiplexer_1 (.sel(R), .in_0(I), .in_1(1'b0), .out(multiplexer_1_out));
  Multiplexer multiplexer_2 (.sel(R), .in_0(C), .in_1(1'b1), .out(multiplexer_2_out));
  D_FF d_ff_1 (.D(multiplexer_1_out), .C(multiplexer_2_out), .Q(Q), .nQ(nQ));
endmodule
