// Digital circuit Draw_condition.dig as structural Verilog
module Draw_condition (
  input  B1,
  input  B2,
  input  B3,
  input  B4,
  input  B5,
  input  B6,
  input  B7,
  input  B8,
  input  B9,
  input  W1,
  input  W2,
  output D,
  output win
);

  wire and_1_out, and_2_out, and_3_out, and_4_out;

  and and_1 (and_1_out, B1, B2, B3);
  and and_2 (and_2_out, B4, B5, B6);
  and and_3 (and_3_out, B7, B8, B9);
  and and_4 (and_4_out, and_1_out, and_2_out, and_3_out);
  xnor xnor_1 (win, W1, W2);
  and and_5 (D, and_4_out, win);
endmodule
