// Digital circuit Led_display.dig as structural Verilog
module Led_display (
);

  wire _1_out, _2_out, _3_out, _4_out, _5_out, _6_out, _7_out, _8_out, _9_out, and_logic_1_f1,
       and_logic_1_f2, and_logic_1_f3, and_logic_1_f4, and_logic_1_f5, and_logic_1_f6, and_logic_1_f7,
       and_logic_1_f8, and_logic_1_f9, draw_condition_1_d, draw_condition_1_win, memory_condition_1_q,
       memory_condition_1_q1, memory_condition_2_q, memory_condition_2_q1, memory_condition_3_q,
       memory_condition_3_q1, memory_condition_4_q, memory_condition_4_q1, memory_condition_5_q,
       memory_condition_5_q1, memory_condition_6_q, memory_condition_6_q1, memory_condition_7_q,
       memory_condition_7_q1, memory_condition_8_q, memory_condition_8_q1, memory_condition_9_q,
       memory_condition_9_q1, RESET_out, win_led_p1, win_led_p3, xor_logic_1_p1, xor_logic_1_p2,
       xor_logic_1_x1, xor_logic_1_x2, xor_logic_1_x3, xor_logic_1_x4, xor_logic_1_x5, xor_logic_1_x6,
       xor_logic_1_x7, xor_logic_1_x8, xor_logic_1_x9;

  Button _1 (.out(_1_out));
  Button _4 (.out(_4_out));
  Button _7 (.out(_7_out));
  Button _2 (.out(_2_out));
  Button _5 (.out(_5_out));
  Button _8 (.out(_8_out));
  and_logic and_logic_1 (
    .W(draw_condition_1_win), .b1(_1_out), .b2(_2_out), .b3(_3_out), .b4(_4_out), .b5(_5_out), .b6(_6_out),
    .b7(_7_out), .b8(_8_out), .b9(_9_out), .f1(and_logic_1_f1), .f2(and_logic_1_f2), .f3(and_logic_1_f3),
    .f4(and_logic_1_f4), .f5(and_logic_1_f5), .f6(and_logic_1_f6), .f7(and_logic_1_f7), .f8(and_logic_1_f8),
    .f9(and_logic_1_f9));
  Button _3 (.out(_3_out));
  Button _6 (.out(_6_out));
  Button _9 (.out(_9_out));
  Button RESET (.out(RESET_out));
  memory_condition memory_condition_1 (
    .P1(xor_logic_1_p1), .P2(xor_logic_1_p2), .Reset(RESET_out), .B_I(and_logic_1_f1),
    .Q(memory_condition_1_q), .Q1(memory_condition_1_q1));
  memory_condition memory_condition_2 (
    .P1(xor_logic_1_p1), .P2(xor_logic_1_p2), .Reset(RESET_out), .B_I(and_logic_1_f2),
    .Q(memory_condition_2_q), .Q1(memory_condition_2_q1));
  memory_condition memory_condition_3 (
    .P1(xor_logic_1_p1), .P2(xor_logic_1_p2), .Reset(RESET_out), .B_I(and_logic_1_f3),
    .Q(memory_condition_3_q), .Q1(memory_condition_3_q1));
  memory_condition memory_condition_4 (
    .P1(xor_logic_1_p1), .P2(xor_logic_1_p2), .Reset(RESET_out), .B_I(and_logic_1_f4),
    .Q(memory_condition_4_q), .Q1(memory_condition_4_q1));
  memory_condition memory_condition_5 (
    .P1(xor_logic_1_p1), .P2(xor_logic_1_p2), .Reset(RESET_out), .B_I(and_logic_1_f5),
    .Q(memory_condition_5_q), .Q1(memory_condition_5_q1));
  memory_condition memory_condition_6 (
    .P1(xor_logic_1_p1), .P2(xor_logic_1_p2), .Reset(RESET_out), .B_I(and_logic_1_f6),
    .Q(memory_condition_6_q), .Q1(memory_condition_6_q1));
  memory_condition memory_condition_7 (
    .P1(xor_logic_1_p1), .P2(xor_logic_1_p2), .Reset(RESET_out), .B_I(and_logic_1_f7),
    .Q(memory_condition_7_q), .Q1(memory_condition_7_q1));
  memory_condition memory_condition_8 (
    .P1(xor_logic_1_p1), .P2(xor_logic_1_p2), .Reset(RESET_out), .B_I(and_logic_1_f8),
    .Q(memory_condition_8_q), .Q1(memory_condition_8_q1));
  memory_condition memory_condition_9 (
    .P1(xor_logic_1_p1), .P2(xor_logic_1_p2), .Reset(RESET_out), .B_I(and_logic_1_f9),
    .Q(memory_condition_9_q), .Q1(memory_condition_9_q1));
  // RGBLED _1_2: pin names not known; wires that end beside it: memory_condition_1_q, 1'b0, memory_condition_1_q1, memory_condition_4_q
  // RGBLED _4_2: pin names not known; wires that end beside it: 1'b0, memory_condition_4_q1, memory_condition_7_q
  // RGBLED _7_2: pin names not known; wires that end beside it: 1'b0, memory_condition_7_q1
  // RGBLED _2_2: pin names not known; wires that end beside it: memory_condition_2_q, 1'b0, memory_condition_2_q1, memory_condition_5_q
  // RGBLED _5_2: pin names not known; wires that end beside it: 1'b0, memory_condition_5_q1, memory_condition_8_q
  // RGBLED _8_2: pin names not known; wires that end beside it: 1'b0, memory_condition_8_q1
  // RGBLED _3_2: pin names not known; wires that end beside it: memory_condition_3_q, 1'b0, memory_condition_3_q1, memory_condition_6_q
  // RGBLED _6_2: pin names not known; wires that end beside it: 1'b0, memory_condition_6_q1, memory_condition_9_q
  // RGBLED _9_2: pin names not known; wires that end beside it: 1'b0, memory_condition_9_q1
  // RGBLED win_led: pin names not known; wires that end beside it: win_led_p1, 1'b0, win_led_p3
  XOR_logic xor_logic_1 (
    .I1(memory_condition_1_q), .I1_2(memory_condition_1_q1), .I2(memory_condition_2_q),
    .I2_2(memory_condition_2_q1), .I3(memory_condition_3_q), .I3_2(memory_condition_3_q1),
    .I4(memory_condition_4_q), .I4_2(memory_condition_4_q1), .I5(memory_condition_5_q),
    .I5_2(memory_condition_5_q1), .I6(memory_condition_6_q), .I6_2(memory_condition_6_q1),
    .I7(memory_condition_7_q), .I7_2(memory_condition_7_q1), .I8(memory_condition_8_q),
    .I8_2(memory_condition_8_q1), .I9(memory_condition_9_q), .I9_2(memory_condition_9_q1),
    .P1(xor_logic_1_p1), .P2(xor_logic_1_p2), .X1(xor_logic_1_x1), .X2(xor_logic_1_x2), .X3(xor_logic_1_x3),
    .X4(xor_logic_1_x4), .X5(xor_logic_1_x5), .X6(xor_logic_1_x6), .X7(xor_logic_1_x7), .X8(xor_logic_1_x8),
    .X9(xor_logic_1_x9));
  winning_condition winning_condition_1 (
    .I1(memory_condition_1_q), .I2(memory_condition_2_q), .I3(memory_condition_3_q),
    .I4(memory_condition_4_q), .I5(memory_condition_5_q), .I6(memory_condition_6_q),
    .I7(memory_condition_7_q), .I8(memory_condition_8_q), .I9(memory_condition_9_q), .W(win_led_p1));
  winning_condition winning_condition_2 (
    .I1(memory_condition_1_q1), .I2(memory_condition_2_q1), .I3(memory_condition_3_q1),
    .I4(memory_condition_4_q1), .I5(memory_condition_5_q1), .I6(memory_condition_6_q1),
    .I7(memory_condition_7_q1), .I8(memory_condition_8_q1), .I9(memory_condition_9_q1), .W(win_led_p3));
  LED draw (.in(draw_condition_1_d));
  Draw_condition draw_condition_1 (
    .B1(xor_logic_1_x1), .B2(xor_logic_1_x2), .B3(xor_logic_1_x3), .B4(xor_logic_1_x4), .B5(xor_logic_1_x5),
    .B6(xor_logic_1_x6), .B7(xor_logic_1_x7), .B8(xor_logic_1_x8), .B9(xor_logic_1_x9), .W1(win_led_p1),
    .W2(win_led_p3), .D(draw_condition_1_d), .win(draw_condition_1_win));
endmodule
