// Digital circuit XOR_logic.dig as structural Verilog
module XOR_logic (
  input  I1,
  input  I1_2,
  input  I2,
  input  I2_2,
  input  I3,
  input  I3_2,
  input  I4,
  input  I4_2,
  input  I5,
  input  I5_2,
  input  I6,
  input  I6_2,
  input  I7,
  input  I7_2,
  input  I8,
  input  I8_2,
  input  I9,
  input  I9_2,
  output P1,
  output P2,
  output X1,
  output X2,
  output X3,
  output X4,
  output X5,
  output X6,
  output X7,
  output X8,
  output X9
);

  wire xor_10_out, xor_11_out, xor_12_out, xor_13_out, xor_14_out, xor_15_out, xor_16_out;

  xor xor_1 (X1, I1, I1_2);
  xor xor_2 (X2, I2, I2_2);
  xor xor_3 (X3, I3, I3_2);
  xor xor_4 (X4, I4, I4_2);
  xor xor_5 (X5, I5, I5_2);
  xor xor_6 (X6, I6, I6_2);
  xor xor_7 (X7, I7, I7_2);
  xor xor_8 (X8, I8, I8_2);
  xor xor_9 (X9, I9, I9_2);
  xor xor_10 (xor_10_out, X1, X2);
  xor xor_11 (xor_11_out, X3, X4);
  xor xor_12 (xor_12_out, X5, X6);
  xor xor_13 (xor_13_out, X7, X8);
  xor xor_14 (xor_14_out, xor_10_out, xor_11_out);
  xor xor_15 (xor_15_out, xor_12_out, xor_13_out);
  xor xor_16 (xor_16_out, xor_14_out, xor_15_out);
  xor xor_17 (P1, xor_16_out, X9);
  not not_1 (P2, P1);
endmodule
