// Digital circuit and_logic.dig as structural Verilog
module and_logic (
  input  W,
  input  b1,
  input  b2,
  input  b3,
  input  b4,
  input  b5,
  input  b6,
  input  b7,
  input  b8,
  input  b9,
  output f1,
  output f2,
  output f3,
  output f4,
  output f5,
  output f6,
  output f7,
  output f8,
  output f9
);

  and and_1 (f1, b1, W);
  and and_2 (f2, b2, W);
  and and_3 (f3, b3, W);
  and and_4 (f4, b4, W);
  and and_5 (f5, b5, W);
  and and_6 (f6, b6, W);
  and and_7 (f7, b7, W);
  and and_8 (f8, b8, W);
  and and_9 (f9, b9, W);
endmodule
