// Digital circuit memory_condition.dig as structural Verilog
module memory_condition (
  input  P1,
  input  P2,
  input  Reset,
  input  B_I,
  output Q,
  output Q1
);

  wire dflip_flop_1_nq, dflip_flop_1_q, dflip_flop_2_nq, dflip_flop_3_nq;

  Dflip_flop dflip_flop_1 (.I(1'b1), .C(B_I), .R(Reset), .Q(dflip_flop_1_q), .nQ(dflip_flop_1_nq));
  Dflip_flop dflip_flop_2 (.I(P1), .C(dflip_flop_1_q), .R(Reset), .Q(Q), .nQ(dflip_flop_2_nq));
  Dflip_flop dflip_flop_3 (.I(P2), .C(dflip_flop_1_q), .R(Reset), .Q(Q1), .nQ(dflip_flop_3_nq));
endmodule
