// Digital circuit winning_condition.dig as structural Verilog
module winning_condition (
  input  I1,
  input  I2,
  input  I3,
  input  I4,
  input  I5,
  input  I6,
  input  I7,
  input  I8,
  input  I9,
  output W
);

  wire and_1_out, and_2_out, and_3_out, and_4_out, and_5_out, and_6_out, and_7_out, and_8_out, or_1_out,
       or_2_out;

  and and_1 (and_1_out, I1, I2, I3);
  and and_2 (and_2_out, I4, I5, I6);
  and and_3 (and_3_out, I7, I8, I9);
  and and_4 (and_4_out, I1, I4, I7);
  and and_5 (and_5_out, I2, I5, I8);
  and and_6 (and_6_out, I3, I6, I9);
  and and_7 (and_7_out, I1, I5, I9);
  and and_8 (and_8_out, I3, I5, I7);
  or or_1 (or_1_out, and_1_out, and_2_out, and_3_out, and_4_out);
  or or_2 (or_2_out, and_5_out, and_6_out, and_7_out, and_8_out);
  or or_3 (W, or_1_out, or_2_out);
endmodule
